# Fritzing sketch Untitled Sketch (saved by Fritzing 0.9.3b)
circuit board: 2.4cm x 3.6cm
circuit board: 6.8765cm x 3.39968cm
breadboards: 1

parts:
  U1 = Voltage Regulator - 5V [package="TO220 [THT]"]
  J1 = female pin header, 2 pins [form="♀ (female)"]
  R1 = Resistor [tolerance=±5% resistance=220 package=THT]
  DS1 = DS18B20 1-Wire Temperature Sensor [part_number=DS18B20]
  MCU1 = Raspberry Pi Zero
  Part1 = Barometric Pressure Sensor - BMP180 Breakout (GY-68)
  J2 = rounded female pin header, 5 pins [form="♀ (female rounded)"]
  Y1 = CRYSTAL [package=hc49u-v]  # not connected

nets:
  N1: U1.input_voltage, J1.pin2
  GND: U1.GND, J1.pin1, DS1.GND, MCU1.pin_6, MCU1.pin_9, MCU1.pin_34, Part1.GND, J2.pin4
  N2: U1.output_voltage, MCU1.pin_2, MCU1.pin_4
  N3: R1.Pin_0, DS1.DQ, MCU1.pin_7
  VDD: R1.Pin_1, DS1.VDD, MCU1.pin_1, MCU1.pin_17, Part1.VCC, J2.pin5
  N4: MCU1.pin_3, Part1.SDA
  N5: MCU1.pin_5, Part1.SCL
  N6: MCU1.pin_8, J2.pin2
  N7: MCU1.pin_10, J2.pin3

notes:
  pps
  rxd
  txd
  gnd
  vcc
